# Fritzing sketch iPhoneControlSplitter (saved by Fritzing 0.9.0b)
breadboards: 1

parts:
  MIC1 = Microphone
  Part1 = Arduino Uno (Rev3)
  C1 = Ceramic Capacitor [capacitance=100nF package="100 mil [THT, multilayer]"]
  R1 = Resistor [tolerance=±5% resistance=2.2k package=THT]
  AA37 = IC, DIP package, 6 pins [chip_label=AA37]
  R2 = Resistor [tolerance=±5% resistance=100k package=THT]
  HA17358 = IC, DIP package, 8 pins [chip_label=358]
  R3 = Resistor [tolerance=±5% resistance=1k package=THT]
  R4 = Resistor [tolerance=±5% resistance=68k package=THT]
  TIP-122 = Voltage Regulator - 5V [package="TO220 [THT]"]
  R5 = Resistor [tolerance=±5% resistance=1k package=THT]
  D1 = Rectifier Diode [part_number=1N4001 package="300 mil [THT]"]
  R6 = Resistor [tolerance=±5% resistance=10k package=THT]
  R7 = Trimmer Potentiometer [maximum_resistance=10kΩ package=THT]
  R8 = Resistor [tolerance=±5% resistance=330 package=THT]
  LED1 = smd LED [color="Red (633nm)" package="1206 [SMD]"]
  Moisture_Sensor = Humidity Sensor - HIH-4030 Breakout
  Pump = DC Motor

nets:
  N1: MIC1.pin1, AA37.pin2, HA17358.pin4, R3.Pin_1, R4.Pin_1, R8.Pin_1
  N2: MIC1.pin2, C1.0, R1.Pin_1
  N3: Part1.A0, Moisture_Sensor.OUT
  N4: Part1.A1, R2.Pin_0, HA17358.pin1
  N5: Part1.D8, LED1.anode
  N6: Part1.D5_PWM, R7.wiper
  N7: Part1.D6_PWM, AA37.pin1, R5.Pin_0, R5.Pin_1
  N8: Part1.RESET, AA37.pin6
  5V: Part1.5V, Moisture_Sensor.VCC
  GND: Part1.GND, Moisture_Sensor.GND
  N9: C1.1, HA17358.pin3, R4.Pin_0
  N10: R1.Pin_0, HA17358.pin8, Pump.pin_1
  N11: AA37.pin5, TIP-122.output_voltage
  N12: R2.Pin_1, HA17358.pin2, R3.Pin_0
  N13: TIP-122.input_voltage, R6.Pin_1
  N14: TIP-122.GND, D1.anode, Pump.pin_2
  N15: R6.Pin_0, R7.leg2
  N16: R8.Pin_0, LED1.cathode
