# Fritzing sketch ArduinoNano with SoftModem (saved by Fritzing 0.9.1b)
circuit board: 8.46667cm x 5.64444cm
breadboards: 1

parts:
  Part1 = Arduino Nano (Rev3.0)
  R1 = Resistor [tolerance=±20% resistance=2k package=THT]
  R2 = Resistor [tolerance=±20% resistance=2k package=THT]
  C2 = Electrolytic Capacitor [capacitance=10µF voltage=50V package="100 mil [THT, electrolytic]"]
  C4 = Ceramic Capacitor [package="100 mil [THT, multilayer]"]
  C5 = Ceramic Capacitor [package="1206 [SMD, multilayer]"]
  C6 = Ceramic Capacitor [package="1206 [SMD, multilayer]"]
  Q1 = NPN-Transistor [package=C9013]
  R3 = Resistor [tolerance=±5% resistance=100k package=THT]
  R4 = Resistor [tolerance=±5% resistance=270 package=THT]
  R5 = Resistor [tolerance=±5% resistance=10k package=THT]
  R6 = Resistor [tolerance=±5% resistance=100k package=THT]
  R7 = Resistor [tolerance=±5% resistance=100k package=THT]
  C7 = Ceramic Capacitor [package="1206 [SMD, multilayer]"]
  C8 = Ceramic Capacitor [package="1206 [SMD, multilayer]"]
  TRRS1 = Audio Jack (TRRS) 3.5mm [part_number="LUMBERG JEITA RC-5325A" package="RC-5325A [SMD]"]  # not connected

nets:
  N1: Part1.GND, R1.Pin_1, R2.Pin_1, C2.+, C4.1, Q1.E, R7.Pin_1
  N2: Part1.D3, R5.Pin_0
  N3: Part1.D6, C4.0, R6.Pin_0, R7.Pin_0, C7.0, C8.0
  N4: Part1.D7, Q1.C, R4.Pin_0
  N5: Part1.5V, R3.Pin_1, R4.Pin_1, R6.Pin_1
  N6: Part1.3V3, C2.-
  N7: R1.Pin_0, C5.0, R5.Pin_1
  N8: R2.Pin_0, C5.1, C6.1
  N9: Q1.B, R3.Pin_0
  N10: C7.1, C8.1

custom parts:
  Ceramic Capacitor: 50 pF multilayer Ceramic Capacitor
  Ceramic Capacitor: 100 nF (104) multilayered Ceramic Capacitor
  NPN-Transistor: A standard NPN-transistor
